// Logisim project Microsequencer.circ as structural Verilog: 1 circuit, main circuit main
module main (
  input  [1:0] select,
  input  [5:0] current_state,
  input  [5:0] valN,
  input  DMemReady,
  input  [3:0] icode,
  input  IMemReady,
  output [5:0] NextState
);

  wire [5:0] bit_extender_1_out, multiplexer_1_out, multiplexer_2_out;

  assign bit_extender_1_out = {{2{1'b1}}, icode};  // Bit_Extender bit_extender_1
  Multiplexer #(.enable("false"), .width(6)) multiplexer_1 (
    .in0(current_state), .in1(valN), .out(multiplexer_1_out), .sel(DMemReady));
  Multiplexer #(.enable("false"), .width(6)) multiplexer_2 (
    .in0(current_state), .in1(bit_extender_1_out), .out(multiplexer_2_out), .sel(IMemReady));
  Multiplexer #(.enable("false"), .select(2), .width(6)) multiplexer_3 (
    .in0(current_state), .in1(valN), .in2(multiplexer_1_out), .in3(multiplexer_2_out), .out(NextState),
    .sel(select));
endmodule
