// Logisim project io-skeleton-2021.circ as structural Verilog: 2 circuits, main circuit io
module io (
  input  KB_Status,
  input  [6:0] KB_Data,
  input  RAM_Use,
  input  RAM_Read,
  input  [31:0] in_5,
  input  TTY_Ready,
  input  [7:0] Incoming_Data,
  input  RAM_Write,
  input  reset,
  output KB_read_enable,
  output KB_Clear,
  output [3:0] out_12,
  output [7:0] Outgoing_Data,
  output [6:0] TTY_Data,
  output [6:0] out_15,
  output TTY_Enable,
  output TTY_Clear
);

  wire and_1_out, and_2_out, and_4_out, and_5_out, and_6_out, comparator_1_lt, comparator_2_lt,
       decoder_1_out0, decoder_1_out1, decoder_1_out2, decoder_1_out3, decoder_1_out4, decoder_1_out5,
       decoder_1_out6, decoder_1_out7, decoder_1_out8, decoder_1_out9, decoder_1_out10, decoder_1_out11,
       decoder_1_out12, decoder_1_out13, decoder_1_out14, decoder_1_out15, not_1_out, or_1_out, or_2_out,
       or_3_out, or_4_out;
  wire [7:0] bit_extender_1_out, bit_extender_2_out, bit_extender_3_out;

  Comparator #(.width(32)) comparator_1 (.a(in_5), .b(32'hfffe00), .lt(comparator_1_lt));  // open: gt, eq
  not not_1 (not_1_out, comparator_1_lt);
  Comparator #(.width(32)) comparator_2 (.a(in_5), .b(32'hfffe0d), .lt(comparator_2_lt));  // open: gt, eq
  BitSelector #(.group(4), .width(32)) bitselector_1 (.in(in_5), .out(out_12), .sel(3'b000));
  and and_1 (and_1_out, not_1_out, comparator_2_lt);
  BitSelector #(.group(7)) bitselector_2 (.in(Incoming_Data), .out(out_15), .sel(1'b0));
  and and_2 (and_2_out, RAM_Use, RAM_Write);
  and and_3 (KB_read_enable, RAM_Use, RAM_Read);
  Decoder #(.select(4)) decoder_1 (
    .out0(decoder_1_out0), .out1(decoder_1_out1), .out2(decoder_1_out2), .out3(decoder_1_out3),
    .out4(decoder_1_out4), .out5(decoder_1_out5), .out6(decoder_1_out6), .out7(decoder_1_out7),
    .out8(decoder_1_out8), .out9(decoder_1_out9), .out10(decoder_1_out10), .out11(decoder_1_out11),
    .out12(decoder_1_out12), .out13(decoder_1_out13), .out14(decoder_1_out14), .out15(decoder_1_out15),
    .sel(out_12), .en(and_1_out));
  or or_1 (or_1_out, decoder_1_out0, decoder_1_out1, decoder_1_out2, decoder_1_out3);
  or or_2 (or_2_out, decoder_1_out4, decoder_1_out5, decoder_1_out6, decoder_1_out7);
  or or_3 (or_3_out, decoder_1_out8, decoder_1_out9, decoder_1_out10, decoder_1_out11);
  or or_4 (or_4_out, decoder_1_out12, decoder_1_out13, decoder_1_out14, decoder_1_out15);
  and and_4 (and_4_out, KB_read_enable, or_1_out);
  and and_5 (and_5_out, KB_read_enable, or_2_out);
  and and_6 (and_6_out, or_3_out, KB_read_enable);
  and and_7 (TTY_Enable, or_4_out, and_2_out);
  assign bit_extender_1_out = {{7{1'b0}}, KB_Status};  // Bit_Extender bit_extender_1
  assign bit_extender_2_out = {{1{1'b0}}, KB_Data};  // Bit_Extender bit_extender_2
  Multiplexer #(.disabled("Z"), .width(8)) multiplexer_1 (
    .in0({8{1'b0}}), .in1(bit_extender_1_out), .out(Outgoing_Data), .sel(KB_Status), .en(and_4_out));
  assign bit_extender_3_out = {{7{1'b0}}, TTY_Ready};  // Bit_Extender bit_extender_3
  Multiplexer #(.disabled("Z"), .width(8)) multiplexer_2 (
    .in0({8{1'b0}}), .in1(bit_extender_2_out), .out(Outgoing_Data), .sel(KB_Status), .en(and_5_out));
  Multiplexer #(.disabled("Z"), .width(8)) multiplexer_3 (
    .in0({8{1'b0}}), .in1(bit_extender_3_out), .out(Outgoing_Data), .sel(TTY_Ready), .en(and_6_out));
  Multiplexer #(.disabled("Z"), .width(7)) multiplexer_4 (
    .in0({7{1'b0}}), .in1(out_15), .out(TTY_Data), .sel(TTY_Ready), .en(TTY_Enable));

  assign KB_Clear = reset;
  assign TTY_Clear = reset;

  // Notes on the sheet:
  //   RAM Address
  //   KBSR
  //   KBDR
  //   DSR
  //   DDR
endmodule

module test (
  input  [1:0] which_register,
  input  [1:0] which_byte,
  input  Use_RAM__please,
  input  read,
  input  write,
  input  in_6
);

  wire clock_out, io_1_kb_clear, io_1_kb_read_enable, io_1_tty_clear, io_1_tty_enable, keyboard_1_avail,
       reset_out;
  wire [6:0] io_1_tty_data, keyboard_1_data;
  wire [7:0] io_1_outgoing_data, register_1_q;
  wire [31:0] adder_1_out, multiplexer_1_out;

  Multiplexer #(.enable("false"), .select(2), .width(32)) multiplexer_1 (
    .in0(32'hfffe00), .in1(32'hfffe04), .in2(32'hfffe08), .in3(32'hfffe0c), .out(multiplexer_1_out),
    .sel(which_register));
  Register register_1 (.Q(register_1_q));  // open: D, en, clk, clr
  // Probe on io_1_outgoing_data
  Register register_2 (.D(io_1_outgoing_data), .clk(clock_out));  // open: en, Q, clr
  // Probe on adder_1_out
  Adder #(.width(32)) adder_1 (
    .a(multiplexer_1_out), .b({{30{1'b0}}, which_byte}), .out(adder_1_out), .cin(1'b0));  // open: cout
  Button reset (.out(reset_out));
  io io_1 (
    .Outgoing_Data(io_1_outgoing_data), .TTY_Data(io_1_tty_data), .KB_read_enable(io_1_kb_read_enable),
    .KB_Clear(io_1_kb_clear), .TTY_Enable(io_1_tty_enable), .TTY_Clear(io_1_tty_clear),
    .KB_Status(keyboard_1_avail), .KB_Data(keyboard_1_data), .TTY_Ready(in_6), .RAM_Use(Use_RAM__please),
    .RAM_Read(read), .in_5(adder_1_out), .Incoming_Data(register_1_q), .RAM_Write(write), .reset(reset_out));  // open: out_12, out_15
  Button clock (.out(clock_out));
  TTY tty_1 (.data(io_1_tty_data), .clk(clock_out), .we(io_1_tty_enable), .clr(io_1_tty_clear));
  Keyboard keyboard_1 (
    .clk(clock_out), .re(io_1_kb_read_enable), .clr(io_1_kb_clear), .avail(keyboard_1_avail),
    .data(keyboard_1_data));

  // Notes on the sheet:
  //   KBSR address
  //   KBDR address
  //   DSR address
  //   DDR address
  //   CPU telling "RAM" what to do
  //   (what the CPU, when reading, captures on clock rise)
  //   data: CPU --> "RAM"
  //   data: "RAM" --> CPU
  //   ----------------------------------------------------------------------------------
  //   "CPU," for your testing
  //   specific byte address
  //   ----------------------------------------------------------------------------------
  //   memory-mapped I/O
  //   (which appears to the CPU as "RAM")
endmodule
