// Logisim project MMU-skeleton.circ as structural Verilog: 2 circuits, main circuit main
module main (
  input  [15:0] Logical_Address,
  input  V,
  input  W,
  input  R,
  input  [7:0] frame_num,
  input  Privilege,
  input  RAM_USE,
  input  READ,
  input  WRITE,
  output [15:0] PHYSICAL_ADDRESS,
  output [7:0] Page_num,
  output RAM_USE_2,
  output READ_2,
  output WRITE_2,
  output EXCEPTION
);

  wire [7:0] Actual_Pagetable_dout;
  wire [10:8] Actual_Pagetable_dout_2;

  RAM #(.dataWidth(11)) Actual_Pagetable (
    .addr(Logical_Address[15:8]), .dout({Actual_Pagetable_dout_2, Actual_Pagetable_dout}));  // open: we, clk, din
  MMU mmu_1 (
    .Exception(EXCEPTION), .Ram_Use__out(RAM_USE_2), .Read__out(READ_2), .Write__out(WRITE_2),
    .Privilege(Privilege), .Ram_Use__in(RAM_USE), .Read__in(READ), .Write__in(WRITE), .Unpriv_Write(W),
    .Unpriv_Read(R), .Valid(V));

  assign Page_num = Logical_Address[15:8];
  assign PHYSICAL_ADDRESS = {frame_num, Logical_Address[7:0]};

  // Notes on the sheet:
  //   (page table entry)
  //   (for testing/demo)
endmodule

module MMU (
  input  Unpriv_Write,
  input  Unpriv_Read,
  input  Valid,
  input  Privilege,
  input  Ram_Use__in,
  input  Read__in,
  input  Write__in,
  output Ram_Use__out,
  output Read__out,
  output Write__out,
  output Exception
);

  wire and_1_out, and_2_out, and_3_out, and_4_out, and_5_out, not_1_out, or_1_out, or_2_out, or_3_out;

  xor xor_1 (Exception, Ram_Use__out, Ram_Use__in);
  not not_1 (not_1_out, Privilege);
  or or_1 (or_1_out, Unpriv_Write, not_1_out);
  or or_2 (or_2_out, Unpriv_Read, not_1_out);
  and and_1 (and_1_out, or_1_out, Write__in);
  and and_2 (and_2_out, or_2_out, Read__in);
  or or_3 (or_3_out, and_2_out, and_1_out);
  and and_3 (and_3_out, Ram_Use__in, or_3_out);
  and and_4 (and_4_out, Read__in, or_2_out);
  and and_5 (and_5_out, Write__in, or_1_out);
  and and_6 (Ram_Use__out, and_3_out, Valid);
  and and_7 (Read__out, and_4_out, Valid);
  and and_8 (Write__out, and_5_out, Valid);

  // Other names for the same wires on the sheet: RAMUSE_IN = Ram_Use__in; RAMUSE_OUT = Ram_Use__out
endmodule
