// Logisim project uarch-skeleton-2021.circ as structural Verilog: 16 circuits, main circuit regwriter
module dpath (
  input  \output ,
  input  Reset,
  output out_3
);

  wire aluBsel, aluOPsel, and_2_out, and_3_out, and_4_out, and_5_out, cnd_1_out_3, comparator_1_eq,
       comparator_2_eq, comparator_3_gt, comparator_4_gt, comparator_5_lt, D_RAMread, D_RAMuse, D_RAMWrite,
       DMemReady, DMemReq, DMemWrite, dstEsel, dstMreq, exception, I_RAMread, I_RAMuse, IMemReady, IMemReq,
       io_1_tty_clear, io_1_tty_enable, kbyte_buddy_1_sel, kbyte_buddy_2_sel, ldCC, ldMAR, ldMDR, ldPC,
       MARsel, MDRsel, multiplexer_10_out, not_1_out, not_2_out, not_3_out, not_4_out, or_1_out, PRIV, RAM,
       regreader_1_clr, regreader_1_clr_2, regreader_1_clr_3, regreader_1_clr_4, regreader_1_clr_5,
       regreader_1_clr_6, regreader_1_clr_7, regreader_1_clr_8, regwriter_1_en, regwriter_1_en_2,
       regwriter_1_en_3, regwriter_1_en_4, regwriter_1_en_5, regwriter_1_en_6, regwriter_1_en_7,
       regwriter_1_en_8, srcAsel, srcBsel, sysreq, sysVal, valCsel;
  wire [1:0] aluAsel, dstEreq, newPCsel, PCIncSel;
  wire [1:1] and_1_out;
  wire [2:0] alu_1_cc, bit_extender_1_out, bit_extender_2_out, bit_extender_3_out, bit_extender_4_out, cc;
  wire [3:0] adder_1_out, icode, ifun, isplit_1_ra, isplit_1_rb, multiplexer_5_out, multiplexer_7_out,
       multiplexer_8_out, multiplexer_9_out, multiplexer_13_out;
  wire [5:0] fsm_1_state;
  wire [6:0] io_1_tty_data;
  wire [7:0] D_Data_from_RAM, D_Data_to_RAM, I_Data_from_RAM, ishim_1_out_6, ishim_1_out_7, ishim_1_out_8,
       ishim_1_out_9, ishim_1_out_10, ishim_1_out_11, ram_1_dout, rom_1_data;
  wire [9:0] kbyte_buddy_1_ram_addr, kbyte_buddy_3_ram_addr;
  wire [10:0] fsm_1_output;
  wire [31:0] adder_2_out, alu_1_vale, D_RAMAddr, dhsim_1_dataout, eax_q, ebp_q, ebx_q, ecx, edi_q, edx_q,
       esi_q, esp_q, I_RAMAddr, isplit_1_d_v, isplit_1_dest, MAR_q, MDR_2_q, multiplexer_1_out,
       multiplexer_2_out, multiplexer_3_out, multiplexer_4_out, multiplexer_6_out, multiplexer_11_out,
       multiplexer_12_out, multiplexer_14_out, multiplexer_15_out, multiplexer_18_out, PC_q,
       regreader_1_vala, regreader_1_valb, regwriter_1_d0, regwriter_1_d1, regwriter_1_d2, regwriter_1_d3,
       regwriter_1_d4, regwriter_1_d5, regwriter_1_d6, regwriter_1_d6_2;

  Register #(.width(32)) PC (.D(multiplexer_3_out), .en(ldPC), .Q(PC_q), .clk(out_3), .clr(Reset));
  Clock Clock (.out(out_3));
  not not_1 (not_1_out, sysVal);
  and and_1 (and_1_out[1], not_1_out, sysreq);
  // Probe on PC_q
  // Probe on I_RAMuse
  // Probe on I_RAMAddr
  // Probe on IMemReq
  // Probe on PCIncSel
  Comparator #(.mode("unsigned"), .width(4)) comparator_1 (
    .a(icode), .b(4'b1101), .eq(comparator_1_eq));  // open: gt, lt
  // Probe on multiplexer_1_out
  Multiplexer #(.enable("false"), .select(2), .width(32)) multiplexer_1 (
    .in0(32'h1), .in1(32'h2), .in2(32'h5), .in3(32'h6), .out(multiplexer_1_out), .sel(PCIncSel));
  // Probe on {and_1_out[1], exception}
  // Probe on cc
  // Probe on I_RAMread
  // Probe on valCsel
  Adder #(.width(4)) adder_1 (.a(icode), .b(ifun), .out(adder_1_out));  // open: cin, cout
  Adder #(.width(32)) adder_2 (.a(multiplexer_1_out), .b(PC_q), .out(adder_2_out), .cin(1'b0));  // open: cout
  Multiplexer #(.enable("false"), .select(2), .width(32)) multiplexer_2 (
    .in0(multiplexer_6_out), .in1(32'h200), .in2(32'h100), .in3(32'h200), .out(multiplexer_2_out),
    .sel({and_1_out[1], exception}));
  CND cnd_1 (.out_3(cnd_1_out_3), .ifun(ifun), .ZSO(cc));
  // Probe on IMemReady
  // Probe on I_Data_from_RAM
  // Probe on srcAsel
  Multiplexer #(.enable("false"), .select(2), .width(32)) multiplexer_3 (
    .in0(adder_2_out), .in1(multiplexer_2_out), .in2(dhsim_1_dataout), .in3(multiplexer_4_out),
    .out(multiplexer_3_out), .sel(newPCsel));
  Multiplexer #(.enable("false"), .width(32)) multiplexer_4 (
    .in0(adder_2_out), .in1(multiplexer_2_out), .out(multiplexer_4_out), .sel(cnd_1_out_3));
  // Probe on cnd_1_out_3
  isplit isplit_1 (
    .Dest(isplit_1_dest), .D_V(isplit_1_d_v), .rA(isplit_1_ra), .rB(isplit_1_rb), .icode(icode), .ifun(ifun),
    .B1(ishim_1_out_7), .B2(ishim_1_out_8), .B3(ishim_1_out_9), .B4(ishim_1_out_10), .B5(ishim_1_out_11),
    .B0(ishim_1_out_6));
  ishim ishim_1 (
    .out_7(ishim_1_out_7), .out_8(ishim_1_out_8), .out_9(ishim_1_out_9), .out_10(ishim_1_out_10),
    .out_11(ishim_1_out_11), .out_6(ishim_1_out_6), .done(IMemReady), .RAMuse(I_RAMuse), .out_14(I_RAMAddr),
    .RAMread(I_RAMread), .in_2(PC_q), .reset(Reset), .req(IMemReq), .clock(out_3), .in_5(I_Data_from_RAM));
  // Probe on srcBsel
  // Probe on dstEsel
  Multiplexer #(.enable("false"), .width(4)) multiplexer_5 (
    .in0(icode), .in1(adder_1_out), .out(multiplexer_5_out), .sel(comparator_1_eq));
  // Probe on icode
  // Probe on ifun
  Multiplexer #(.enable("false"), .width(32)) multiplexer_6 (
    .in0(isplit_1_dest), .in1(isplit_1_d_v), .out(multiplexer_6_out), .sel(valCsel));
  // Probe on multiplexer_6_out
  // Probe on dstEreq
  // Probe on isplit_1_ra
  // Probe on isplit_1_rb
  // Probe on dstMreq
  // Probe on multiplexer_5_out
  Multiplexer #(.enable("false"), .width(4)) multiplexer_7 (
    .in0(isplit_1_rb), .in1(4'b0100), .out(multiplexer_7_out), .sel(dstEsel));
  Multiplexer #(.enable("false"), .width(4)) multiplexer_8 (
    .in0(isplit_1_ra), .in1(4'b0100), .out(multiplexer_8_out), .sel(srcAsel));
  Multiplexer #(.enable("false"), .width(4)) multiplexer_9 (
    .in0(isplit_1_rb), .in1(4'b0100), .out(multiplexer_9_out), .sel(srcBsel));
  // Probe on aluAsel
  // Probe on bit_extender_1_out
  Bit_Extender #(.in_width(4), .out_width(3), .\type ("zero")) bit_extender_1 (
    .in(multiplexer_7_out), .out(bit_extender_1_out));
  Multiplexer #(.enable("false"), .select(2)) multiplexer_10 (
    .in0(1'b0), .in1(1'b1), .in2(cnd_1_out_3), .out(multiplexer_10_out), .sel(dstEreq));  // open: in3
  // Probe on bit_extender_2_out
  Bit_Extender #(.in_width(4), .out_width(3), .\type ("zero")) bit_extender_2 (
    .in(isplit_1_ra), .out(bit_extender_2_out));
  // Probe on dstMreq
  Bit_Extender #(.in_width(4), .out_width(3), .\type ("zero")) bit_extender_3 (
    .in(multiplexer_8_out), .out(bit_extender_3_out));
  Bit_Extender #(.in_width(4), .out_width(3), .\type ("zero")) bit_extender_4 (
    .in(multiplexer_9_out), .out(bit_extender_4_out));
  Comparator #(.width(4)) comparator_2 (.a(multiplexer_9_out), .b(4'b1111), .eq(comparator_2_eq));  // open: gt, lt
  // Probe on aluBsel
  // Probe on {IMemReq, PCIncSel, valCsel, srcAsel, srcBsel, dstEsel, dstEreq, dstMreq, aluAsel, aluBsel, aluOPsel, ldCC, MARsel, ldMAR, MDRsel, ldMDR, DMemReq, DMemWrite, fsm_1_output}
  FSM fsm_1 (
    .\output ({IMemReq, PCIncSel, valCsel, srcAsel, srcBsel, dstEsel, dstEreq, dstMreq, aluAsel, aluBsel, aluOPsel, ldCC, MARsel, ldMAR, MDRsel, ldMDR, DMemReq, DMemWrite, fsm_1_output}),
    .state(fsm_1_state), .reset(Reset), .DMemDone(DMemReady), .IMemDone(IMemReady), .clock(out_3),
    .icode(multiplexer_5_out));
  Register #(.width(1)) register_1 (.D(sysVal), .en(sysreq), .Q(PRIV), .clk(out_3), .clr(Reset));
  Register #(.width(32)) eax (.D(regwriter_1_d0), .en(regwriter_1_en), .Q(eax_q), .clk(out_3), .clr(regreader_1_clr));
  regwriter regwriter_1 (
    .D5(regwriter_1_d5), .EN_6(regwriter_1_en_6), .D6(regwriter_1_d6), .D4(regwriter_1_d4),
    .EN_5(regwriter_1_en_5), .D0(regwriter_1_d0), .EN_7(regwriter_1_en_7), .EN(regwriter_1_en),
    .D1(regwriter_1_d1), .EN_2(regwriter_1_en_2), .D2(regwriter_1_d2), .EN_3(regwriter_1_en_3),
    .D3(regwriter_1_d3), .D6_2(regwriter_1_d6_2), .EN_8(regwriter_1_en_8), .EN_4(regwriter_1_en_4),
    .reqE(multiplexer_10_out), .reqM(dstMreq), .dstE(bit_extender_1_out), .dstM(bit_extender_2_out),
    .valE(alu_1_vale), .valM(dhsim_1_dataout));
  Register #(.width(32)) u_ecx (
    .D(regwriter_1_d1), .en(regwriter_1_en_2), .Q(ecx), .clk(out_3), .clr(regreader_1_clr_2));
  Register #(.width(32)) edx (
    .D(regwriter_1_d2), .en(regwriter_1_en_3), .Q(edx_q), .clk(out_3), .clr(regreader_1_clr_3));
  Register #(.width(32)) ebx (
    .D(regwriter_1_d3), .en(regwriter_1_en_4), .Q(ebx_q), .clk(out_3), .clr(regreader_1_clr_4));
  Register #(.width(32)) esp (
    .D(regwriter_1_d4), .en(regwriter_1_en_5), .Q(esp_q), .clk(out_3), .clr(regreader_1_clr_5));
  Register #(.width(32)) ebp (
    .D(regwriter_1_d5), .en(regwriter_1_en_6), .Q(ebp_q), .clk(out_3), .clr(regreader_1_clr_6));
  Register #(.width(32)) esi (
    .D(regwriter_1_d6), .en(regwriter_1_en_7), .Q(esi_q), .clk(out_3), .clr(regreader_1_clr_7));
  Register #(.width(32)) edi (
    .D(regwriter_1_d6_2), .en(regwriter_1_en_8), .Q(edi_q), .clk(out_3), .clr(regreader_1_clr_8));
  // Probe on aluOPsel
  // Probe on fsm_1_state
  // Probe on PRIV
  regreader regreader_1 (
    .CLR_5(regreader_1_clr_5), .CLR_6(regreader_1_clr_6), .CLR_7(regreader_1_clr_7),
    .CLR_8(regreader_1_clr_8), .CLR(regreader_1_clr), .CLR_2(regreader_1_clr_2), .CLR_3(regreader_1_clr_3),
    .CLR_4(regreader_1_clr_4), .valA(regreader_1_vala), .valB(regreader_1_valb), .Q_5(esp_q), .Q_6(ebp_q),
    .Q_7(esi_q), .Q_8(edi_q), .Q(eax_q), .Q_2(ecx), .Q_3(edx_q), .Q_4(ebx_q), .reset(Reset),
    .srcA(bit_extender_3_out), .srcB(bit_extender_4_out));
  // Probe on ldCC
  // Probe on MARsel
  // Probe on fsm_1_state
  // Probe on regreader_1_vala
  // Probe on regreader_1_valb
  // Probe on multiplexer_6_out
  // Probe on MDRsel
  // Probe on ldMAR
  Multiplexer #(.enable("false"), .select(2), .width(32)) multiplexer_11 (
    .in0(regreader_1_vala), .in1(multiplexer_6_out), .in2(32'h4), .in3(32'hfffffffc),
    .out(multiplexer_11_out), .sel(aluAsel));
  // Probe on multiplexer_11_out
  // Probe on multiplexer_12_out
  Multiplexer #(.enable("false"), .width(32)) multiplexer_12 (
    .in0(regreader_1_valb), .in1({32{1'b0}}), .out(multiplexer_12_out), .sel(or_1_out));
  or or_1 (or_1_out, comparator_2_eq, aluBsel);
  Multiplexer #(.enable("false"), .width(4)) multiplexer_13 (
    .in0(4'b0000), .in1(ifun), .out(multiplexer_13_out), .sel(aluOPsel));
  // Probe on ldMDR
  // Probe on fsm_1_output[8]
  // Probe on fsm_1_output[7]
  // Probe on fsm_1_output[6]
  // Probe on exception
  // Probe on fsm_1_output[8:6]
  alu alu_1 (
    .valE(alu_1_vale), .CC(alu_1_cc), .aluOP(multiplexer_13_out), .aluA(multiplexer_11_out),
    .aluB(multiplexer_12_out));
  // Probe on multiplexer_13_out
  // Probe on DMemReq
  // Probe on cc
  Register #(.width(3)) u_CC (.D(alu_1_cc), .en(ldCC), .Q(cc), .clk(out_3), .clr(Reset));
  // Probe on DMemWrite
  // Probe on adder_2_out
  // Probe on alu_1_vale
  Multiplexer #(.enable("false"), .width(32)) multiplexer_14 (
    .in0(regreader_1_vala), .in1(adder_2_out), .out(multiplexer_14_out), .sel(MDRsel));
  Multiplexer #(.enable("false"), .width(32)) multiplexer_15 (
    .in0(alu_1_vale), .in1(regreader_1_vala), .out(multiplexer_15_out), .sel(MARsel));
  // Probe on newPCsel
  // Probe on ldPC
  or or_2 (ldPC, fsm_1_output[8], exception);
  or or_3 (sysreq, fsm_1_output[7], exception);
  Multiplexer #(.enable("false"), .width(2)) multiplexer_16 (
    .in0(fsm_1_output[10:9]), .in1(2'b01), .out(newPCsel), .sel(exception));
  Comparator #(.width(32)) comparator_3 (.a(D_RAMAddr), .b(32'h400), .gt(comparator_3_gt));  // open: eq, lt
  // Probe on MDR_2_q
  Register #(.width(32)) MDR_2 (.D(multiplexer_14_out), .en(ldMDR), .Q(MDR_2_q), .clk(out_3), .clr(Reset));
  Register #(.width(32)) MAR (.D(multiplexer_15_out), .en(ldMAR), .Q(MAR_q), .clk(out_3), .clr(Reset));
  // Probe on MAR_q
  Multiplexer #(.enable("false")) multiplexer_17 (.in0(fsm_1_output[6]), .in1(1'b0), .out(sysVal), .sel(exception));
  and and_2 (and_2_out, comparator_3_gt, D_RAMuse);
  // Probe on D_RAMAddr
  // Probe on D_RAMuse
  // Probe on D_RAMAddr
  not not_2 (not_2_out, PRIV);
  // Probe on dhsim_1_dataout
  // Probe on D_RAMread
  // Probe on D_RAMWrite
  // Probe on D_Data_to_RAM
  kbyte_buddy kbyte_buddy_1 (
    .ram_addr(kbyte_buddy_1_ram_addr), .sel(kbyte_buddy_1_sel), .addr(D_RAMAddr), .addr_prefix({32{1'b0}}),
    .\use (D_RAMuse));
  kbyte_buddy kbyte_buddy_2 (
    .ram_addr(kbyte_buddy_1_ram_addr), .sel(kbyte_buddy_2_sel), .addr(I_RAMAddr), .addr_prefix({32{1'b0}}),
    .\use (I_RAMuse));
  kbyte_buddy kbyte_buddy_3 (
    .ram_addr(kbyte_buddy_3_ram_addr), .sel(RAM), .addr(D_RAMAddr), .addr_prefix(32'h400), .\use (and_2_out));
  and and_3 (and_3_out, D_RAMuse, not_2_out);
  not not_3 (not_3_out, not_2_out);
  dhsim dhsim_1 (
    .out_9(D_Data_to_RAM), .RAMwrite(D_RAMWrite), .RAMread(D_RAMread), .done(DMemReady),
    .DataOut(dhsim_1_dataout), .RAMuse(D_RAMuse), .out_14(D_RAMAddr), .in_2(D_Data_from_RAM), .in_1(MAR_q),
    .DMem_Write(DMemWrite), .req(DMemReq), .reset(Reset), .clock(out_3), .in_3(MDR_2_q));
  // Probe on D_Data_from_RAM
  not not_4 (not_4_out, RAM);
  // Probe on kbyte_buddy_1_ram_addr
  // Probe on kbyte_buddy_3_ram_addr
  // Probe on D_RAMWrite
  // Probe on D_Data_to_RAM
  // Probe on D_RAMAddr
  Multiplexer #(.enable("false"), .width(32)) multiplexer_18 (
    .in0({32{1'b0}}), .in1(D_RAMAddr), .out(multiplexer_18_out), .sel(and_4_out));
  and and_4 (and_4_out, not_3_out, D_RAMuse);
  // Probe on dhsim_1_dataout
  // Probe on DMemReady
  ROM #(.addrWidth(10)) rom_1 (.addr(kbyte_buddy_1_ram_addr), .data(rom_1_data));
  RAM #(.addrWidth(10)) ram_1 (
    .addr(kbyte_buddy_3_ram_addr), .we(D_RAMWrite), .clk(out_3), .din(D_Data_to_RAM), .dout(ram_1_dout));
  io io_1 (
    .Outgoing_Data(D_Data_from_RAM), .TTY_Data(io_1_tty_data), .TTY_Enable(io_1_tty_enable),
    .TTY_Clear(io_1_tty_clear), .TTY_Ready(1'b1), .RAM_Use(and_3_out), .RAM_Read(D_RAMread),
    .in_5(D_RAMAddr), .Incoming_Data(D_Data_to_RAM), .RAM_Write(D_RAMWrite), .reset(Reset));  // open: KB_read_enable, KB_Clear, KB_Status, KB_Data
  // Probe on D_Data_to_RAM
  and and_5 (and_5_out, not_4_out, D_RAMread);
  Comparator #(.mode("unsigned"), .width(32)) comparator_4 (
    .a(multiplexer_18_out), .b(32'hfffdff), .gt(comparator_4_gt));  // open: eq, lt
  Comparator #(.mode("unsigned"), .width(32)) comparator_5 (
    .a(multiplexer_18_out), .b(32'hffff00), .lt(comparator_5_lt));  // open: gt, eq
  // Probe on ecx
  Multiplexer #(.disabled("Z"), .width(8)) multiplexer_19 (
    .in1(rom_1_data), .out(D_Data_from_RAM), .sel(and_5_out), .en(kbyte_buddy_1_sel));  // open: in0
  Multiplexer #(.disabled("Z"), .width(8)) multiplexer_20 (
    .in1(rom_1_data), .out(I_Data_from_RAM), .sel(kbyte_buddy_2_sel), .en(I_RAMread));  // open: in0
  Multiplexer #(.disabled("Z"), .width(8)) multiplexer_21 (
    .in1(ram_1_dout), .out(D_Data_from_RAM), .sel(RAM), .en(D_RAMread));  // open: in0
  // Probe on io_1_tty_data
  TTY tty_1 (.data(io_1_tty_data), .clk(out_3), .we(io_1_tty_enable), .clr(io_1_tty_clear));
  and and_6 (exception, comparator_4_gt, comparator_5_lt);
  // Probe on D_Data_from_RAM

  // Other names for the same wires on the sheet: Clock = out_3

  // Notes on the sheet:
  //   If sysreq is asserted 
  //   and the new value is 0
  //   (i.e.) attempt to sysenter),
  //   load 0x100 to valC and
  //   if newPCSel is 01 
  //   (should be the case if 
  //   it's a valid sysenter attempt),
  //   then load valC into PC 
  //   Y86 Skeleton
  //   Feb 11, 2021
  //   connect to memory!
  //   Fetch
  //   valP
  //   valM
  //   IR[1:4]
  //   IR[2:5]
  //   Decode/Write-Back
  //   SWS and Taylor Cathcart and Vijay Kothari, based on a skeleton from Matt Kretchmar
  //   PRIV MODE: 0 is privileged
  //   rB == F?
  //   Execute
  //   0 add
  //   Memory
  //   PC
  //   connect to memory (and io,
  //    pretending to be memory)
  //   contents of rom_1 (hex, n*v repeats v):
  //   30 f4 fc 4 0 0 30 f2 d 2 0 0 80 d 1 0 0 d0 70 0 3 235*0 30 f2 12 2 0 0 80 d 1 0 0 d0 90 30 f6 4*0 30
  //   f7 1 0 0 0 30 f3 ff 0 0 0 50 2 4*0 62 30 73 38 1 0 0 80 39 1 0 0 60 72 70 1f 1 0 0 90 50 1f 8 fe ff
  //   0 60 61 73 39 1 0 0 40 f c fe ff 0 90 179*0 30 f2 18 2 0 0 80 d 1 0 0 d0 90 48 69 21 20 0 59 65 73
  //   3f 20 0 55 68 2d 6f 68 21 20 225*0 d1 10 10 e0 10
endmodule

module isplit (
  input  [7:0] B0,
  input  [7:0] B1,
  input  [7:0] B2,
  input  [7:0] B3,
  input  [7:0] B4,
  input  [7:0] B5,
  output [3:0] icode,
  output [3:0] ifun,
  output [3:0] rA,
  output [3:0] rB,
  output [31:0] Dest,
  output [31:0] D_V
);


  assign D_V = {B5, B4, B3, B2};
  assign Dest = {B4, B3, B2, B1};
  assign icode = B0[7:4];
  assign ifun = B0[3:0];
  assign rA = B1[7:4];
  assign rB = B1[3:0];
endmodule

module regreader (
  input  [2:0] srcA,
  input  [2:0] srcB,
  input  [31:0] Q,
  input  [31:0] Q_2,
  input  [31:0] Q_3,
  input  reset,
  input  [31:0] Q_4,
  input  [31:0] Q_5,
  input  [31:0] Q_6,
  input  [31:0] Q_7,
  input  [31:0] Q_8,
  output CLR,
  output [31:0] valA,
  output CLR_2,
  output [31:0] valB,
  output CLR_3,
  output CLR_4,
  output CLR_5,
  output CLR_6,
  output CLR_7,
  output CLR_8
);

  Multiplexer #(.enable("false"), .select(3), .width(32)) multiplexer_1 (
    .in0(Q), .in1(Q_2), .in2(Q_3), .in3(Q_4), .in4(Q_5), .in5(Q_6), .in6(Q_7), .in7(Q_8), .out(valA),
    .sel(srcA));
  Multiplexer #(.enable("false"), .select(3), .width(32)) multiplexer_2 (
    .in0(Q), .in1(Q_2), .in2(Q_3), .in3(Q_4), .in4(Q_5), .in5(Q_6), .in6(Q_7), .in7(Q_8), .out(valB),
    .sel(srcB));

  assign CLR = reset;
  assign CLR_2 = reset;
  assign CLR_3 = reset;
  assign CLR_4 = reset;
  assign CLR_5 = reset;
  assign CLR_6 = reset;
  assign CLR_7 = reset;
  assign CLR_8 = reset;

  // Notes on the sheet:
  //   for reg 0
  //   for reg 7
endmodule

module regwriter (
  input  [2:0] dstE,
  input  reqE,
  input  [2:0] dstM,
  input  reqM,
  input  [31:0] valE,
  input  [31:0] valM,
  output [31:0] D0,
  output EN,
  output [31:0] D1,
  output EN_2,
  output [31:0] D2,
  output EN_3,
  output [31:0] D3,
  output EN_4,
  output [31:0] D4,
  output EN_5,
  output [31:0] D5,
  output EN_6,
  output [31:0] D6,
  output EN_7,
  output [31:0] D6_2,
  output EN_8
);

  wire demultiplexer_2_out0, demultiplexer_2_out1, demultiplexer_2_out2, demultiplexer_2_out3,
       demultiplexer_2_out4, demultiplexer_2_out5, demultiplexer_2_out6, demultiplexer_2_out7,
       demultiplexer_4_out0, demultiplexer_4_out1, demultiplexer_4_out2, demultiplexer_4_out3,
       demultiplexer_4_out4, demultiplexer_4_out5, demultiplexer_4_out6, demultiplexer_4_out7,
       selector_1_write_to, selector_2_write_to, selector_3_write_to, selector_4_write_to,
       selector_5_write_to, selector_6_write_to, selector_7_write_to, selector_8_write_to;
  wire [31:0] demultiplexer_1_out0, demultiplexer_1_out1, demultiplexer_1_out2, demultiplexer_1_out3,
       demultiplexer_1_out4, demultiplexer_1_out5, demultiplexer_1_out6, demultiplexer_1_out7,
       demultiplexer_3_out0, demultiplexer_3_out1, demultiplexer_3_out2, demultiplexer_3_out3,
       demultiplexer_3_out4, demultiplexer_3_out5, demultiplexer_3_out6, demultiplexer_3_out7;

  Demultiplexer #(.enable("false"), .select(3), .width(32)) demultiplexer_1 (
    .out0(demultiplexer_1_out0), .out1(demultiplexer_1_out1), .out2(demultiplexer_1_out2),
    .out3(demultiplexer_1_out3), .out4(demultiplexer_1_out4), .out5(demultiplexer_1_out5),
    .out6(demultiplexer_1_out6), .out7(demultiplexer_1_out7), .in(valM), .sel(dstM));
  Demultiplexer #(.enable("false"), .select(3)) demultiplexer_2 (
    .out0(demultiplexer_2_out0), .out1(demultiplexer_2_out1), .out2(demultiplexer_2_out2),
    .out3(demultiplexer_2_out3), .out4(demultiplexer_2_out4), .out5(demultiplexer_2_out5),
    .out6(demultiplexer_2_out6), .out7(demultiplexer_2_out7), .in(reqE), .sel(dstE));
  Demultiplexer #(.enable("false"), .select(3), .width(32)) demultiplexer_3 (
    .out0(demultiplexer_3_out0), .out1(demultiplexer_3_out1), .out2(demultiplexer_3_out2),
    .out3(demultiplexer_3_out3), .out4(demultiplexer_3_out4), .out5(demultiplexer_3_out5),
    .out6(demultiplexer_3_out6), .out7(demultiplexer_3_out7), .in(valE), .sel(dstE));
  Demultiplexer #(.enable("false"), .select(3)) demultiplexer_4 (
    .out0(demultiplexer_4_out0), .out1(demultiplexer_4_out1), .out2(demultiplexer_4_out2),
    .out3(demultiplexer_4_out3), .out4(demultiplexer_4_out4), .out5(demultiplexer_4_out5),
    .out6(demultiplexer_4_out6), .out7(demultiplexer_4_out7), .in(reqM), .sel(dstM));
  selector selector_1 (
    .write_to(selector_1_write_to), .enable(EN), .in_1(demultiplexer_2_out0), .in_2(demultiplexer_4_out0));
  selector selector_2 (
    .write_to(selector_2_write_to), .enable(EN_2), .in_1(demultiplexer_2_out1), .in_2(demultiplexer_4_out1));
  selector selector_3 (
    .write_to(selector_3_write_to), .enable(EN_3), .in_1(demultiplexer_2_out2), .in_2(demultiplexer_4_out2));
  selector selector_4 (
    .write_to(selector_4_write_to), .enable(EN_4), .in_1(demultiplexer_2_out3), .in_2(demultiplexer_4_out3));
  selector selector_5 (
    .write_to(selector_5_write_to), .enable(EN_5), .in_1(demultiplexer_2_out4), .in_2(demultiplexer_4_out4));
  selector selector_6 (
    .write_to(selector_6_write_to), .enable(EN_6), .in_1(demultiplexer_2_out5), .in_2(demultiplexer_4_out5));
  selector selector_7 (
    .write_to(selector_7_write_to), .enable(EN_7), .in_1(demultiplexer_2_out6), .in_2(demultiplexer_4_out6));
  selector selector_8 (
    .write_to(selector_8_write_to), .enable(EN_8), .in_1(demultiplexer_2_out7), .in_2(demultiplexer_4_out7));
  Multiplexer #(.enable("false"), .width(32)) multiplexer_1 (
    .in0(demultiplexer_3_out0), .in1(demultiplexer_1_out0), .out(D0), .sel(selector_1_write_to));
  Multiplexer #(.enable("false"), .width(32)) multiplexer_2 (
    .in0(demultiplexer_3_out1), .in1(demultiplexer_1_out1), .out(D1), .sel(selector_2_write_to));
  Multiplexer #(.enable("false"), .width(32)) multiplexer_3 (
    .in0(demultiplexer_3_out2), .in1(demultiplexer_1_out2), .out(D2), .sel(selector_3_write_to));
  Multiplexer #(.enable("false"), .width(32)) multiplexer_4 (
    .in0(demultiplexer_3_out3), .in1(demultiplexer_1_out3), .out(D3), .sel(selector_4_write_to));
  Multiplexer #(.enable("false"), .width(32)) multiplexer_5 (
    .in0(demultiplexer_3_out4), .in1(demultiplexer_1_out4), .out(D4), .sel(selector_5_write_to));
  Multiplexer #(.enable("false"), .width(32)) multiplexer_6 (
    .in0(demultiplexer_3_out5), .in1(demultiplexer_1_out5), .out(D5), .sel(selector_6_write_to));
  Multiplexer #(.enable("false"), .width(32)) multiplexer_7 (
    .in0(demultiplexer_3_out6), .in1(demultiplexer_1_out6), .out(D6), .sel(selector_7_write_to));
  Multiplexer #(.enable("false"), .width(32)) multiplexer_8 (
    .in0(demultiplexer_3_out7), .in1(demultiplexer_1_out7), .out(D6_2), .sel(selector_8_write_to));
endmodule

module aluOLD (
  input  [31:0] aluA,
  input  [31:0] aluB,
  input  [3:0] aluOP,
  input  [3:0] aluOP_2,
  output [2:0] CC,
  output [2:0] CC_2,
  output [31:0] valE,
  output [31:0] valE_2
);

  wire adder_1_cout, bitselector_1_out, bitselector_2_out, bitselector_3_out, or_1_out, subtractor_1_bout;
  wire [31:0] adder_1_out, and_1_out, subtractor_1_out, undriven, undriven_2, xor_1_out;

  BitSelector #(.width(32)) bitselector_1 (.in(undriven), .out(bitselector_1_out), .sel({5{1'b1}}));
  BitSelector #(.width(32)) bitselector_2 (.in(undriven_2), .out(bitselector_2_out), .sel({5{1'b1}}));
  Adder #(.width(32)) adder_1 (.a(undriven_2), .b(undriven), .out(adder_1_out), .cout(adder_1_cout));  // open: cin
  Subtractor #(.width(32)) subtractor_1 (
    .a(undriven_2), .b(undriven), .out(subtractor_1_out), .bout(subtractor_1_bout));  // open: bin
  assign and_1_out = undriven_2 & undriven;  // AND_Gate and_1, 32 bits wide
  assign xor_1_out = undriven_2 ^ undriven;  // XOR_Gate xor_1, 32 bits wide
  or or_1 (or_1_out, bitselector_1_out, bitselector_2_out);
  Multiplexer #(.enable("false"), .select(4), .width(32)) multiplexer_1 (
    .in0(adder_1_out), .in1(subtractor_1_out), .in2(and_1_out), .in3(xor_1_out), .in4({32{1'b0}}),
    .in5({32{1'b0}}), .in6({32{1'b0}}), .in7({32{1'b0}}), .in8({32{1'b0}}), .in9({32{1'b0}}),
    .in10({32{1'b0}}), .in11({32{1'b0}}), .in12({32{1'b0}}), .in13({32{1'b0}}), .in14({32{1'b0}}),
    .in15({32{1'b0}}), .out(valE), .sel(aluOP_2));
  BitSelector #(.width(32)) bitselector_3 (.in(valE), .out(bitselector_3_out), .sel({5{1'b1}}));
  xor xor_2 (CC[2], bitselector_3_out, or_1_out);
  Comparator #(.width(32)) comparator_1 (.a({32{1'b0}}), .b(valE), .eq(CC[0]));  // open: gt, lt
  BitSelector #(.width(32)) bitselector_4 (.in(valE), .out(CC[1]), .sel({5{1'b1}}));

  // Notes on the sheet:
  //   add
  //   subtract
  //   AND
  //   XOR
  //   over max using addl
  //   [Z,S,O]
endmodule

module alu (
  input  [31:0] aluA,
  input  [31:0] aluB,
  input  [3:0] aluOP,
  output [2:0] CC,
  output [31:0] valE
);

  wire adder_1_cout, bitselector_1_out, bitselector_2_out, bitselector_3_out, or_1_out, subtractor_1_bout;
  wire [31:0] adder_1_out, and_1_out, subtractor_1_out, xor_1_out;

  BitSelector #(.width(32)) bitselector_1 (.in(aluA), .out(bitselector_1_out), .sel({5{1'b1}}));
  BitSelector #(.width(32)) bitselector_2 (.in(aluB), .out(bitselector_2_out), .sel({5{1'b1}}));
  Adder #(.width(32)) adder_1 (.a(aluB), .b(aluA), .out(adder_1_out), .cout(adder_1_cout));  // open: cin
  Subtractor #(.width(32)) subtractor_1 (
    .a(aluB), .b(aluA), .out(subtractor_1_out), .bout(subtractor_1_bout));  // open: bin
  assign and_1_out = aluB & aluA;  // AND_Gate and_1, 32 bits wide
  assign xor_1_out = aluB ^ aluA;  // XOR_Gate xor_1, 32 bits wide
  or or_1 (or_1_out, bitselector_1_out, bitselector_2_out);
  Multiplexer #(.enable("false"), .select(4), .width(32)) multiplexer_1 (
    .in0(adder_1_out), .in1(subtractor_1_out), .in2(and_1_out), .in3(xor_1_out), .in4({32{1'b0}}),
    .in5({32{1'b0}}), .in6({32{1'b0}}), .in7({32{1'b0}}), .in8({32{1'b0}}), .in9({32{1'b0}}),
    .in10({32{1'b0}}), .in11({32{1'b0}}), .in12({32{1'b0}}), .in13({32{1'b0}}), .in14({32{1'b0}}),
    .in15({32{1'b0}}), .out(valE), .sel(aluOP));
  BitSelector #(.width(32)) bitselector_3 (.in(valE), .out(bitselector_3_out), .sel({5{1'b1}}));
  xor xor_2 (CC[2], bitselector_3_out, or_1_out);
  Comparator #(.width(32)) comparator_1 (.a({32{1'b0}}), .b(valE), .eq(CC[0]));  // open: gt, lt
  BitSelector #(.width(32)) bitselector_4 (.in(valE), .out(CC[1]), .sel({5{1'b1}}));

  // Notes on the sheet:
  //   add
  //   subtract
  //   AND
  //   XOR
endmodule

module MSB (
  input  [31:0] Value,
  output MSB
);


  assign MSB = Value[31];
endmodule

module CND (
  input  [2:0] ZSO,
  input  [3:0] ifun,
  output out_3
);

  wire and_1_out, and_2_out, not_1_out, not_2_out, not_3_out, or_1_out;

  and and_1 (and_1_out, ZSO[0], ZSO[1]);
  not not_1 (not_1_out, ZSO[2]);
  not not_2 (not_2_out, and_1_out);
  not not_3 (not_3_out, ZSO[2]);
  and and_2 (and_2_out, not_2_out, not_3_out);
  or or_1 (or_1_out, and_1_out, ZSO[2]);
  Multiplexer #(.enable("false"), .select(4)) multiplexer_1 (
    .in0(1'b1), .in1(or_1_out), .in2(and_1_out), .in3(ZSO[2]), .in4(not_1_out), .in5(not_2_out),
    .in6(and_2_out), .in7(1'b0), .in8(1'b0), .in9(1'b0), .in10(1'b0), .in11(1'b0), .in12(1'b0), .in13(1'b0),
    .in14(1'b0), .in15(1'b0), .out(out_3), .sel(ifun));

  // Notes on the sheet:
  //   Z
  //   S
  //   O
endmodule

module ishim (
  input  req,
  input  [31:0] in_2,
  input  reset,
  input  clock,
  input  [7:0] in_5,
  output [7:0] out_6,
  output [7:0] out_7,
  output [7:0] out_8,
  output [7:0] out_9,
  output [7:0] out_10,
  output [7:0] out_11,
  output done,
  output RAMuse,
  output [31:0] out_14,
  output RAMread
);

  wire decoder_1_out0, decoder_1_out1, decoder_1_out2, decoder_1_out3, decoder_1_out4, decoder_1_out5,
       decoder_1_out6, or_1_out;
  wire [2:0] counter_1_q;
  wire [31:0] adder_1_out, bit_extender_1_out;

  D_Flip_Flop #(.enable("true")) d_ff_1 (
    .clk(clock), .D(req), .Q(RAMread), .Qn(done), .preset(1'b0), .en(done), .reset(or_1_out));
  Decoder #(.select(3)) decoder_1 (
    .out0(decoder_1_out0), .out1(decoder_1_out1), .out2(decoder_1_out2), .out3(decoder_1_out3),
    .out4(decoder_1_out4), .out5(decoder_1_out5), .out6(decoder_1_out6), .sel(counter_1_q), .en(RAMread));  // open: out7
  Counter #(.max('h7), .width(3)) counter_1 (
    .load(1'b0), .count(RAMread), .Q(counter_1_q), .up(1'b1), .clk(clock), .clr(or_1_out));  // open: D, carry
  or or_1 (or_1_out, decoder_1_out6, reset);
  assign bit_extender_1_out = {{29{1'b0}}, counter_1_q};  // Bit_Extender bit_extender_1
  Adder #(.width(32)) adder_1 (.a(in_2), .b(bit_extender_1_out), .out(adder_1_out), .cin(1'b0));  // open: cout
  assign out_14 = RAMread ? adder_1_out : 32'bz;  // Controlled_Buffer controlled_buffer_1
  Register #(.trigger("falling")) register_1 (.D(in_5), .en(decoder_1_out0), .Q(out_6), .clk(clock), .clr(reset));
  Register #(.trigger("falling")) register_2 (.D(in_5), .en(decoder_1_out1), .Q(out_7), .clk(clock), .clr(reset));
  Register #(.trigger("falling")) register_3 (.D(in_5), .en(decoder_1_out2), .Q(out_8), .clk(clock), .clr(reset));
  Register #(.trigger("falling")) register_4 (.D(in_5), .en(decoder_1_out3), .Q(out_9), .clk(clock), .clr(reset));
  Register #(.trigger("falling")) register_5 (.D(in_5), .en(decoder_1_out4), .Q(out_10), .clk(clock), .clr(reset));
  Register #(.trigger("falling")) register_6 (.D(in_5), .en(decoder_1_out5), .Q(out_11), .clk(clock), .clr(reset));

  assign RAMuse = RAMread;

  // Notes on the sheet:
  //   addr
  //   in use?
  //   state
  //   (3 bits)
  //   RAMaddr (32 bits)
  //   data from RAM (8 bits)
  //   byte 0
  //   byte 1
  //   byte 2
  //   byte 3
  //   byte 4
  //   byte 5
endmodule

module dhsim (
  input  [31:0] in_1,
  input  [7:0] in_2,
  input  [31:0] in_3,
  input  DMem_Write,
  input  req,
  input  reset,
  input  clock,
  output [31:0] DataOut,
  output [7:0] out_9,
  output RAMwrite,
  output RAMread,
  output done,
  output RAMuse,
  output [31:0] out_14
);

  wire comparator_1_eq, d_ff_1_q, d_ff_1_qn, decoder_1_out0, decoder_1_out1, decoder_1_out2, decoder_1_out3,
       or_1_out;
  wire [1:0] bit_extender_2_out;
  wire [2:0] counter_1_q;
  wire [31:0] adder_1_out, bit_extender_1_out;

  assign bit_extender_1_out = {{29{1'b0}}, counter_1_q};  // Bit_Extender bit_extender_1
  D_Flip_Flop #(.enable("true")) d_ff_1 (
    .clk(clock), .D(DMem_Write), .Q(d_ff_1_q), .Qn(d_ff_1_qn), .preset(1'b0), .en(done), .reset(reset));
  D_Flip_Flop #(.enable("true")) in_use (
    .clk(clock), .D(req), .Q(RAMuse), .Qn(done), .preset(1'b0), .en(done), .reset(or_1_out));
  Adder #(.width(32)) adder_1 (.a(in_1), .b(bit_extender_1_out), .out(adder_1_out), .cin(1'b0));  // open: cout
  and and_1 (RAMwrite, RAMuse, d_ff_1_q);
  and and_2 (RAMread, d_ff_1_qn, RAMuse);
  Decoder #(.select(3)) decoder_1 (
    .out0(decoder_1_out0), .out1(decoder_1_out1), .out2(decoder_1_out2), .out3(decoder_1_out3),
    .sel(counter_1_q), .en(RAMread));  // open: out4, out5, out6, out7
  Counter #(.max('h7), .width(3)) counter_1 (
    .load(1'b0), .count(RAMuse), .Q(counter_1_q), .up(1'b1), .clk(clock), .clr(or_1_out));  // open: D, carry
  or or_1 (or_1_out, comparator_1_eq, reset);
  Comparator #(.mode("unsigned"), .width(3)) comparator_1 (
    .a(counter_1_q), .b(3'b100), .eq(comparator_1_eq));  // open: gt, lt
  assign out_14 = RAMuse ? adder_1_out : 32'bz;  // Controlled_Buffer controlled_buffer_1
  Bit_Extender #(.in_width(3), .out_width(2)) bit_extender_2 (.in(counter_1_q), .out(bit_extender_2_out));
  Multiplexer #(.select(2), .width(8)) multiplexer_1 (
    .in0(in_3[7:0]), .in1(in_3[15:8]), .in2(in_3[23:16]), .in3(in_3[31:24]), .out(out_9),
    .sel(bit_extender_2_out), .en(RAMwrite));
  Register #(.trigger("falling")) register_1 (
    .D(in_2), .en(decoder_1_out0), .Q(DataOut[7:0]), .clk(clock), .clr(reset));
  Register #(.trigger("falling")) register_2 (
    .D(in_2), .en(decoder_1_out1), .Q(DataOut[15:8]), .clk(clock), .clr(reset));
  Register #(.trigger("falling")) register_3 (
    .D(in_2), .en(decoder_1_out2), .Q(DataOut[23:16]), .clk(clock), .clr(reset));
  Register #(.trigger("falling")) register_4 (
    .D(in_2), .en(decoder_1_out3), .Q(DataOut[31:24]), .clk(clock), .clr(reset));

  // Notes on the sheet:
  //   address
  //   writing?
  //   reading?
  //   state
  //   (3 bits)
  //   data in
  //   RAMaddr (32 bits)
  //   data from RAM (8 bits)
  //   data to RAM (8 bits)
endmodule

module io (
  input  KB_Status,
  input  [6:0] KB_Data,
  input  RAM_Use,
  input  RAM_Read,
  input  [31:0] in_5,
  input  TTY_Ready,
  input  [7:0] Incoming_Data,
  input  RAM_Write,
  input  reset,
  output KB_read_enable,
  output KB_Clear,
  output [7:0] Outgoing_Data,
  output [6:0] TTY_Data,
  output TTY_Enable,
  output TTY_Clear
);

  wire and_1_out, and_2_out, and_3_out, and_4_out, and_6_out, comparator_1_lt, comparator_2_lt,
       decoder_1_out0, decoder_1_out1, decoder_1_out2, decoder_1_out3, decoder_1_out4, decoder_1_out5,
       decoder_1_out6, decoder_1_out7, decoder_1_out8, decoder_1_out9, decoder_1_out10, decoder_1_out11,
       decoder_1_out12, decoder_1_out13, decoder_1_out14, decoder_1_out15, not_1_out, or_1_out, or_2_out,
       or_3_out, or_4_out;
  wire [3:0] bitselector_1_out;
  wire [6:0] bitselector_2_out;
  wire [7:0] bit_extender_1_out, bit_extender_2_out, bit_extender_3_out;

  Comparator #(.width(32)) comparator_1 (.a(in_5), .b(32'hfffe00), .lt(comparator_1_lt));  // open: gt, eq
  not not_1 (not_1_out, comparator_1_lt);
  Comparator #(.width(32)) comparator_2 (.a(in_5), .b(32'hfffe0f), .lt(comparator_2_lt));  // open: gt, eq
  BitSelector #(.group(4), .width(32)) bitselector_1 (.in(in_5), .out(bitselector_1_out), .sel(3'b000));
  and and_1 (and_1_out, not_1_out, comparator_2_lt);
  BitSelector #(.group(7)) bitselector_2 (.in(Incoming_Data), .out(bitselector_2_out), .sel(1'b0));
  and and_2 (and_2_out, RAM_Use, RAM_Write);
  and and_3 (and_3_out, RAM_Use, RAM_Read);
  Decoder #(.select(4)) decoder_1 (
    .out0(decoder_1_out0), .out1(decoder_1_out1), .out2(decoder_1_out2), .out3(decoder_1_out3),
    .out4(decoder_1_out4), .out5(decoder_1_out5), .out6(decoder_1_out6), .out7(decoder_1_out7),
    .out8(decoder_1_out8), .out9(decoder_1_out9), .out10(decoder_1_out10), .out11(decoder_1_out11),
    .out12(decoder_1_out12), .out13(decoder_1_out13), .out14(decoder_1_out14), .out15(decoder_1_out15),
    .sel(bitselector_1_out), .en(and_1_out));
  or or_1 (or_1_out, decoder_1_out0, decoder_1_out1, decoder_1_out2, decoder_1_out3);
  or or_2 (or_2_out, decoder_1_out4, decoder_1_out5, decoder_1_out6, decoder_1_out7);
  or or_3 (or_3_out, decoder_1_out8, decoder_1_out9, decoder_1_out10, decoder_1_out11);
  or or_4 (or_4_out, decoder_1_out12, decoder_1_out13, decoder_1_out14, decoder_1_out15);
  and and_4 (and_4_out, and_3_out, or_1_out);
  and and_5 (KB_read_enable, and_3_out, or_2_out);
  and and_6 (and_6_out, or_3_out, and_3_out);
  and and_7 (TTY_Enable, or_4_out, and_2_out);
  assign bit_extender_1_out = {{7{1'b0}}, KB_Status};  // Bit_Extender bit_extender_1
  assign bit_extender_2_out = {{1{1'b0}}, KB_Data};  // Bit_Extender bit_extender_2
  Multiplexer #(.disabled("Z"), .width(8)) multiplexer_1 (
    .in0({8{1'b0}}), .in1(bit_extender_1_out), .out(Outgoing_Data), .sel(KB_Status), .en(and_4_out));
  assign bit_extender_3_out = {{7{1'b0}}, TTY_Ready};  // Bit_Extender bit_extender_3
  Multiplexer #(.disabled("Z"), .width(8)) multiplexer_2 (
    .in0({8{1'b0}}), .in1(bit_extender_2_out), .out(Outgoing_Data), .sel(KB_Status), .en(KB_read_enable));
  Multiplexer #(.disabled("Z"), .width(8)) multiplexer_3 (
    .in0({8{1'b0}}), .in1(bit_extender_3_out), .out(Outgoing_Data), .sel(TTY_Ready), .en(and_6_out));
  Multiplexer #(.disabled("Z"), .width(7)) multiplexer_4 (
    .in0({7{1'b0}}), .in1(bitselector_2_out), .out(TTY_Data), .sel(TTY_Ready), .en(TTY_Enable));

  assign KB_Clear = reset;
  assign TTY_Clear = reset;

  // Notes on the sheet:
  //   RAM Address
  //   KBSR
  //   KBDR
  //   DSR
  //   DDR
endmodule

module kbyte_buddy (
  input  [31:0] addr,
  input  [31:0] addr_prefix,
  input  \use ,
  output [9:0] ram_addr,
  output sel
);

  wire comparator_1_eq;
  wire [31:0] and_1_out;

  Bit_Extender #(.in_width(32), .out_width(10), .\type ("zero")) bit_extender_1 (.in(addr), .out(ram_addr));
  assign and_1_out = addr & 32'hfffffc00;  // AND_Gate and_1, 32 bits wide
  Comparator #(.mode("unsigned"), .width(32)) comparator_1 (
    .a(and_1_out), .b(addr_prefix), .eq(comparator_1_eq));  // open: gt, lt
  and and_2 (sel, comparator_1_eq, \use );
endmodule

module FSM (
  input  clock,
  input  reset,
  input  [3:0] icode,
  input  DMemDone,
  input  IMemDone,
  output [31:0] \output ,
  output [5:0] state
);

  wire [1:0] s;
  wire [3:0] rom_2_data;
  wire [5:0] microsequencer_1_nextstate, valN;

  // Probe on state
  // Probe on state
  // Probe on state
  ROM #(.addrWidth(6), .dataWidth(32)) rom_1 (.addr(state), .data(\output ));
  ROM #(.addrWidth(6), .dataWidth(12)) rom_2 (.addr(state), .data({s, valN, rom_2_data}));
  microsequencer microsequencer_1 (
    .NextState(microsequencer_1_nextstate), .select(s), .current_state(state), .valN(valN),
    .DMemReady(DMemDone), .icode(icode), .IMemReady(IMemDone));
  Register #(.width(6)) register_1 (.D(microsequencer_1_nextstate), .Q(state), .clk(clock), .clr(reset));  // open: en
  // Probe on valN
  // Probe on s

  // Other names for the same wires on the sheet: CurrentState[5:0] = state; DMemReady = DMemDone;
  //   IMemReady = IMemDone

  // Notes on the sheet:
  //   contents of rom_1 (hex, n*v repeats v):
  //   80000000 0 1800 0 0 0 1000 1000 400000 500 39*0 100 21080100 70980100 7010a100 70108100 30860100
  //   40000700 46b0e300 ea18000 26b0a100 2ea18100 70960100 1c0 6b0e380
  //   contents of rom_2 (hex, n*v repeats v):
  //   410 c10 430 800 880 890 440 450 400 400 39*0 400 400 400 420 460 400 400 420 470 420 460 400 400 420
endmodule

module microsequencer (
  input  [1:0] select,
  input  [5:0] current_state,
  input  [5:0] valN,
  input  DMemReady,
  input  [3:0] icode,
  input  IMemReady,
  output [5:0] NextState
);

  wire [5:0] bit_extender_1_out, multiplexer_1_out, multiplexer_2_out;

  assign bit_extender_1_out = {{2{1'b1}}, icode};  // Bit_Extender bit_extender_1
  Multiplexer #(.enable("false"), .width(6)) multiplexer_1 (
    .in0(current_state), .in1(valN), .out(multiplexer_1_out), .sel(DMemReady));
  Multiplexer #(.enable("false"), .width(6)) multiplexer_2 (
    .in0(current_state), .in1(bit_extender_1_out), .out(multiplexer_2_out), .sel(IMemReady));
  Multiplexer #(.enable("false"), .select(2), .width(6)) multiplexer_3 (
    .in0(current_state), .in1(valN), .in2(multiplexer_1_out), .in3(multiplexer_2_out), .out(NextState),
    .sel(select));
endmodule

module selector (
  input  in_1,
  input  in_2,
  output write_to,
  output enable
);

  wire and_1_out, comparator_1_eq, comparator_1_gt, not_1_out, or_1_out, transistor_1_out;

  Comparator #(.width(1)) comparator_1 (.a(in_1), .b(in_2), .gt(comparator_1_gt), .eq(comparator_1_eq));  // open: lt
  or or_1 (or_1_out, comparator_1_gt, and_1_out);
  and and_1 (and_1_out, comparator_1_eq, in_2);
  Transistor #(.\type ("n")) transistor_1 (.in(or_1_out), .out(transistor_1_out), .gate(in_1));
  Transistor #(.gate("br")) transistor_2 (.in(or_1_out), .out(transistor_1_out), .gate(not_1_out));
  not not_1 (not_1_out, in_2);
  or or_2 (enable, in_1, in_2);
  and and_2 (write_to, transistor_1_out, or_1_out);
endmodule

module iotest (
  input  \output ,
  input  output_2,
  input  output_3,
  input  [7:0] output_4,
  input  output_5
);

  wire clock_1_out, io_1_tty_clear, io_1_tty_enable;
  wire [6:0] io_1_tty_data;

  Clock clock_1 (.out(clock_1_out));
  io io_1 (
    .TTY_Data(io_1_tty_data), .TTY_Enable(io_1_tty_enable), .TTY_Clear(io_1_tty_clear), .TTY_Ready(1'b1),
    .RAM_Use(\output ), .RAM_Read(output_2), .in_5(32'hfffe0c), .Incoming_Data(output_4),
    .RAM_Write(output_3), .reset(output_5));  // open: Outgoing_Data, KB_read_enable, KB_Clear, KB_Status, KB_Data
  TTY tty_1 (.data(io_1_tty_data), .clk(clock_1_out), .we(io_1_tty_enable), .clr(io_1_tty_clear));
endmodule
